// Logisim project control-logic.circ as structural Verilog: 1 circuit, main circuit control_logic
module control_logic (
  input  [31:0] inst,
  input  BrEq,
  input  BrLt,
  output PCSel,
  output RegWEn,
  output [2:0] ImmSel,
  output BrUn,
  output ASel,
  output BSel,
  output [3:0] ALUSel,
  output MemRW,
  output [1:0] WBSel,
  output CSRSel,
  output CSRWen
);

  wire add_or_auipc, and_1_out, and_2_out, and_3_out, and_4_out, and_5_out, and_6_out, comparator_1_eq,
       comparator_2_eq, comparator_7_eq, comparator_8_eq, comparator_9_eq, comparator_10_eq, decoder_3_out5,
       decoder_4_out0, decoder_4_out1, decoder_4_out5, is_add, is_addi, is_and, is_andi, is_auipc, is_beq,
       is_bge, is_bgeu, is_blt, is_bltu, is_bne, is_csrw, is_csrwi, is_jal, is_jalr, is_lb, is_lh, is_lui,
       is_lw, is_mul, is_mulh, is_mulhu, is_or, is_ori, is_sb, is_sh, is_sll, is_slli, is_slt, is_slti,
       is_sra, is_srai, is_srl, is_srli, is_sub, is_sw, is_xor, is_xori, mul_or_lui, mulh_or_csrw,
       mulhu_or_csrwi, not_1_out, not_2_out, not_3_out, sll_or_jalr, sub_or_jal;
  wire [5:0] ROM_input;

  ROM #(.addrWidth(6), .dataWidth(16)) rom_1 (
    .addr(ROM_input), .data({RegWEn, ImmSel, BrUn, ASel, BSel, ALUSel, MemRW, WBSel, CSRSel, CSRWen}));
  Comparator #(.mode("unsigned"), .width(7)) comparator_1 (
    .a(7'b0100011), .b(inst[6:0]), .eq(comparator_1_eq));  // open: gt, lt
  Comparator #(.mode("unsigned"), .width(7)) comparator_2 (
    .a(7'b1100011), .b(inst[6:0]), .eq(comparator_2_eq));  // open: gt, lt
  Comparator #(.mode("unsigned"), .width(7)) comparator_3 (
    .a(7'b0010111), .b(inst[6:0]), .eq(is_auipc));  // open: gt, lt
  Comparator #(.mode("unsigned"), .width(7)) comparator_4 (.a(7'b0110111), .b(inst[6:0]), .eq(is_lui));  // open: gt, lt
  Comparator #(.mode("unsigned"), .width(7)) comparator_5 (.a(7'b1101111), .b(inst[6:0]), .eq(is_jal));  // open: gt, lt
  Comparator #(.mode("unsigned"), .width(7)) comparator_6 (
    .a(7'b1100111), .b(inst[6:0]), .eq(is_jalr));  // open: gt, lt
  Decoder #(.select(2)) decoder_1 (
    .out0(is_sb), .out1(is_sh), .out2(is_sw), .sel(inst[13:12]), .en(comparator_1_eq));  // open: out3
  Decoder #(.select(3)) decoder_2 (
    .out0(is_beq), .out1(is_bne), .out4(is_blt), .out5(is_bge), .out6(is_bltu), .out7(is_bgeu),
    .sel(inst[14:12]), .en(comparator_2_eq));  // open: out2, out3
  and and_1 (and_1_out, is_beq, BrEq);
  and and_2 (and_2_out, is_bne, not_1_out);
  not not_1 (not_1_out, BrEq);
  and and_3 (and_3_out, is_blt, BrLt);
  and and_4 (and_4_out, is_bge, not_2_out);
  not not_2 (not_2_out, BrLt);
  and and_5 (and_5_out, is_bltu, BrLt);
  and and_6 (and_6_out, is_bgeu, not_3_out);
  not not_3 (not_3_out, BrLt);
  Comparator #(.mode("unsigned"), .width(7)) comparator_7 (
    .a(7'b0110011), .b(inst[6:0]), .eq(comparator_7_eq));  // open: gt, lt
  Comparator #(.mode("unsigned"), .width(7)) comparator_8 (
    .a(7'b0000011), .b(inst[6:0]), .eq(comparator_8_eq));  // open: gt, lt
  Decoder #(.select(3)) decoder_3 (
    .out0(is_addi), .out1(is_slli), .out2(is_slti), .out4(is_xori), .out5(decoder_3_out5), .out6(is_ori),
    .out7(is_andi), .sel(inst[14:12]), .en(comparator_9_eq));  // open: out3
  Comparator #(.mode("unsigned"), .width(7)) comparator_9 (
    .a(7'b0010011), .b(inst[6:0]), .eq(comparator_9_eq));  // open: gt, lt
  Decoder #(.select(3)) decoder_4 (
    .out0(decoder_4_out0), .out1(decoder_4_out1), .out2(is_slt), .out3(is_mulhu), .out4(is_xor),
    .out5(decoder_4_out5), .out6(is_or), .out7(is_and), .sel(inst[14:12]), .en(comparator_7_eq));
  Decoder #(.select(2)) decoder_5 (
    .out0(is_lb), .out1(is_lh), .out2(is_lw), .sel(inst[13:12]), .en(comparator_8_eq));  // open: out3
  or or_1 (PCSel, is_jalr, and_1_out, and_2_out, and_3_out, and_4_out, and_5_out, and_6_out, is_jal);
  Decoder decoder_6 (.out0(is_srli), .out1(is_srai), .sel(inst[30]), .en(decoder_3_out5));
  Decoder #(.select(2)) decoder_7 (
    .out0(is_add), .out1(is_mul), .out2(is_sub), .sel({inst[30], inst[25]}), .en(decoder_4_out0));  // open: out3
  Decoder decoder_8 (.out0(is_sll), .out1(is_mulh), .sel(inst[25]), .en(decoder_4_out1));
  Decoder decoder_9 (.out0(is_srl), .out1(is_sra), .sel(inst[30]), .en(decoder_4_out5));
  Decoder decoder_10 (.out0(is_csrw), .out1(is_csrwi), .sel(inst[14]), .en(comparator_10_eq));
  Comparator #(.mode("unsigned"), .width(7)) comparator_10 (
    .a(7'b1110011), .b(inst[6:0]), .eq(comparator_10_eq));  // open: gt, lt
  Priority_Encoder #(.select(5)) priority_encoder_1 (
    .in0(add_or_auipc), .in1(mul_or_lui), .in2(sub_or_jal), .in3(sll_or_jalr), .in4(mulh_or_csrw),
    .in5(mulhu_or_csrwi), .in6(is_slt), .in7(is_xor), .in8(is_srl), .in9(is_sra), .in10(is_or),
    .in11(is_and), .in12(is_lb), .in13(is_lh), .in14(is_lw), .in15(is_addi), .in16(is_slli), .in17(is_slti),
    .in18(is_xori), .in19(is_srli), .in20(is_srai), .in21(is_ori), .in22(is_andi), .in23(is_sb),
    .in24(is_sh), .in25(is_sw), .in26(is_beq), .in27(is_bne), .in28(is_blt), .in29(is_bge), .in30(is_bltu),
    .in31(is_bgeu), .out(ROM_input[4:0]));  // open: gs, en_out, en_in
  or or_2 (add_or_auipc, is_add, is_auipc);
  or or_3 (mul_or_lui, is_mul, is_lui);
  or or_4 (sub_or_jal, is_sub, is_jal);
  or or_5 (sll_or_jalr, is_sll, is_jalr);
  or or_6 (mulh_or_csrw, is_mulh, is_csrw);
  or or_7 (mulhu_or_csrwi, is_mulhu, is_csrwi);
  or or_8 (ROM_input[5], is_auipc, is_lui, is_jal, is_jalr, is_csrw, is_csrwi);

  // Other names for the same wires on the sheet: Opcode[6:0] = inst[6:0]; funct3[2:0] = inst[14:12];
  //   funct7[6:0] = inst[31:25]

  // Notes on the sheet:
  //   INPUTS to your circuit
  //   contents of rom_1 (hex, n*v repeats v):
  //   f004 f104 f184 f024 f124 f164 f044 f084 f0a4 f1a4 f0c4 f0e4 8200 8200 8200 8204 8224 8244 8284 82a4
  //   83a4 82c4 82e4 121c 121c 121c 4*260c 2e0c 2e0c b604 b3e4 c608 8208 500d 500f
  //   ROM FOR CONTROL LOGIC
  //   S Type
  //   B Type
  //   auipc
  //   lui
  //   jal
  //   jalr
  //   DON'T CHANGE THE LOCATIONS OF THE INPUTS AND OUTPUTS!
  //   OUTPUT from your circuit
  //   R Type Decoder
  //   Load Word
  //   Other I Type
  //   CSR Type
endmodule
