// Logisim project cpu.circ as structural Verilog: 1 circuit, main circuit cpu
module cpu (
  input  clk,
  input  [31:0] INSTRUCTION,
  input  [31:0] MEM_READ_DATA,
  output [31:0] MEM_WRITE_ADDRESS,
  output [31:0] PROGRAM_COUNTER,
  output [31:0] ra,
  output [31:0] sp,
  output [31:0] t0,
  output [31:0] t1,
  output [31:0] t2,
  output [31:0] s0,
  output [31:0] s1,
  output [31:0] a0,
  output [31:0] tohost,
  output [3:0] MEM_WRITE_ENABLE,
  output [31:0] MEM_WRITE_DATA
);

  wire ASel, BrEq, BrLt, BrUn, BSel, CSRSel, CSRWen, MemRW, PCSel, RegWEn;
  wire [1:0] WBSel;
  wire [2:0] funct3, ImmSel;
  wire [3:0] ALUSel, multiplexer_8_out;
  wire [7:0] multiplexer_6_out;
  wire [15:0] multiplexer_7_out;
  wire [31:0] adder_1_out, bit_extender_1_out, bit_extender_2_out, imm, INSTRUCTION_t, multiplexer_1_out,
       multiplexer_2_out, multiplexer_3_out, multiplexer_4_out, multiplexer_5_out, multiplexer_10_out,
       PC_PLUS_FOUR, PROGRAM_COUNTER_t, read_data1, write_data;

  Adder #(.width(32)) adder_1 (.a(PROGRAM_COUNTER), .b(32'h4), .out(adder_1_out));  // open: cin, cout
  Register #(.width(32)) PC_REGISTER (.D(PROGRAM_COUNTER), .clk(clk), .Q(PROGRAM_COUNTER_t));  // open: en, clr
  Multiplexer #(.enable("false"), .width(32)) multiplexer_1 (
    .in0(adder_1_out), .in1(MEM_WRITE_ADDRESS), .out(multiplexer_1_out), .sel(PCSel));
  Register #(.width(32)) PC (.D(multiplexer_1_out), .clk(clk), .Q(PROGRAM_COUNTER));  // open: en, clr
  Register #(.width(32)) INSTRUCTION_REGISTER (
    .D(multiplexer_2_out), .clk(clk), .Q({INSTRUCTION_t[31:15], funct3, INSTRUCTION_t[11:0]}));  // open: en, clr
  Multiplexer #(.enable("false"), .width(32)) multiplexer_2 (
    .in0(INSTRUCTION), .in1(32'h13), .out(multiplexer_2_out), .sel(PCSel));
  Adder #(.width(32)) adder_2 (.a(PROGRAM_COUNTER_t), .b(32'h4), .out(PC_PLUS_FOUR));  // open: cin, cout
  control_logic control_logic_1 (
    .CSRWen(CSRWen), .PCSel(PCSel), .RegWEn(RegWEn), .ImmSel(ImmSel), .BrUn(BrUn), .ASel(ASel), .BSel(BSel),
    .ALUSel(ALUSel), .MemRW(MemRW), .WBSel(WBSel), .CSRSel(CSRSel),
    .inst({INSTRUCTION_t[31:15], funct3, INSTRUCTION_t[11:0]}), .BrEq(BrEq), .BrLt(BrLt));
  regfile regfile_1 (
    .rs1(INSTRUCTION_t[19:15]), .rs2(INSTRUCTION_t[24:20]), .rd(INSTRUCTION_t[11:7]),
    .Write_Data(write_data), .RegWEn(RegWEn), .clk(clk), .ra(ra), .sp(sp), .t0(t0), .t1(t1), .t2(t2),
    .s0(s0), .s1(s1), .a0(a0), .Read_Data_1(read_data1), .Read_Data_2(MEM_WRITE_DATA));
  branch_comp branch_comp_1 (.rs1(read_data1), .rs2(MEM_WRITE_DATA), .BrUn(BrUn), .BrEq(BrEq), .BrLt(BrLt));
  imm_gen imm_gen_1 (.inst({INSTRUCTION_t[31:15], funct3, INSTRUCTION_t[11:0]}), .ImmSel(ImmSel), .imm(imm));
  Multiplexer #(.enable("false"), .width(32)) multiplexer_3 (
    .in0(read_data1), .in1(imm), .out(multiplexer_3_out), .sel(CSRSel));
  Multiplexer #(.enable("false"), .width(32)) multiplexer_4 (
    .in0(read_data1), .in1(PROGRAM_COUNTER_t), .out(multiplexer_4_out), .sel(ASel));
  Multiplexer #(.enable("false"), .width(32)) multiplexer_5 (
    .in0(MEM_WRITE_DATA), .in1(imm), .out(multiplexer_5_out), .sel(BSel));
  alu alu_1 (.Result(MEM_WRITE_ADDRESS), .A(multiplexer_4_out), .B(multiplexer_5_out), .ALUSel(ALUSel));
  // csr csr_1: pin names not known; wires that end beside it: INSTRUCTION_t[31:20], multiplexer_3_out, CSRWen, clk, tohost
  assign bit_extender_1_out = {{24{multiplexer_6_out[7]}}, multiplexer_6_out};  // Bit_Extender bit_extender_1
  Multiplexer #(.enable("false"), .select(2), .width(8)) multiplexer_6 (
    .in0(MEM_READ_DATA[7:0]), .in1(MEM_READ_DATA[15:8]), .in2(MEM_READ_DATA[23:16]),
    .in3(MEM_READ_DATA[31:24]), .out(multiplexer_6_out), .sel(MEM_WRITE_ADDRESS[1:0]));
  assign bit_extender_2_out = {{16{multiplexer_7_out[15]}}, multiplexer_7_out};  // Bit_Extender bit_extender_2
  Multiplexer #(.enable("false"), .width(16)) multiplexer_7 (
    .in0(MEM_READ_DATA[15:0]), .in1(MEM_READ_DATA[31:16]), .out(multiplexer_7_out), .sel(MEM_WRITE_ADDRESS[1]));
  Multiplexer #(.enable("false"), .select(4), .width(4)) multiplexer_8 (
    .in0(4'b0001), .in1(4'b0010), .in2(4'b0100), .in3(4'b1000), .in4(4'b0011), .in6(4'b1100), .in8(4'b1111),
    .out(multiplexer_8_out), .sel({funct3[1:0], MEM_WRITE_ADDRESS[1:0]}));  // open: in5, in7, in9, in10, in11, in12, in13, in14, in15
  Multiplexer #(.enable("false"), .width(4)) multiplexer_9 (
    .in0(4'b0000), .in1(multiplexer_8_out), .out(MEM_WRITE_ENABLE), .sel(MemRW));
  Multiplexer #(.enable("false"), .select(2), .width(32)) multiplexer_10 (
    .in0(bit_extender_1_out), .in1(bit_extender_2_out), .in2(MEM_READ_DATA), .out(multiplexer_10_out),
    .sel(funct3[1:0]));  // open: in3
  Multiplexer #(.enable("false"), .select(2), .width(32)) multiplexer_11 (
    .in0(multiplexer_10_out), .in1(MEM_WRITE_ADDRESS), .in2(PC_PLUS_FOUR), .out(write_data), .sel(WBSel));  // open: in3

  // Other names for the same wires on the sheet: ALU_Output[31:0] = MEM_WRITE_ADDRESS; INSTRUCTION_t[14:12] = funct3;
  //   write_reg[4:0] = INSTRUCTION_t[11:7]; read_reg1[4:0] = INSTRUCTION_t[19:15];
  //   read_reg2[4:0] = INSTRUCTION_t[24:20]; NEXT_INSTRUCTION[31:0] = INSTRUCTION;
  //   NEXT_PROGRAM_COUNTER[31:0] = PROGRAM_COUNTER; read_data2[31:0] = MEM_WRITE_DATA

  // Notes on the sheet:
  //   Output to IMEM
  //   IMEM (do **NOT** move this)
  //   Inputs from IMEM
  //   It is OK to move the PC, RegFile, ALU, MEM, Branch Comp, Imm Gen, and Control Logic to wherever is most convenient for you when constructing your CPU, and to delete this text
  //   Inputs/Outputs for testing. Do **NOT** move these.
  //   Outputs To DMEM
  //   DMEM (do **NOT** move this)
  //   Inputs From DMEM
endmodule
